// Logisim project p22_localtest_0.circ as structural Verilog: 1 circuit, main circuit main
module main (
  input  rst,
  output [7:0] out_2,
  output [31:0] current_pc_if,
  output mem_wen_mem,
  output halt,
  output [31:0] mem_din_mem,
  output [31:0] mem_dout_mem,
  output [31:0] mem_addr_mem,
  output control_en_mem,
  output [31:0] control_pc_mem,
  output wb_en_wb,
  output [4:0] wb_addr_wb,
  output [31:0] wb_data_wb
);

  wire and_1_out, carry, clk, not_1_out, not_2_out, por_1_out, rst_t;
  wire [31:0] inst;

  not not_1 (not_1_out, inst[2]);
  not not_2 (not_2_out, inst[3]);
  POR por_1 (.out(por_1_out));
  TOP top_1 (
    .clk(clk), .rst(rst_t), .inst(inst), .current_pc_if(current_pc_if), .mem_wen_mem(mem_wen_mem),
    .mem_din_mem(mem_din_mem), .mem_dout_mem(mem_dout_mem), .mem_addr_mem(mem_addr_mem),
    .control_en_mem(control_en_mem), .control_pc_mem(control_pc_mem), .wb_en_wb(wb_en_wb),
    .wb_addr_wb(wb_addr_wb), .wb_data_wb(wb_data_wb));
  Clock clock_1 (.out(clk));
  or or_1 (rst_t, rst, por_1_out);
  and and_1 (and_1_out, inst[0], inst[1], not_1_out, not_2_out, inst[4], inst[5], inst[6]);
  or or_2 (halt, and_1_out, carry);
  Counter counter_1 (.clr(rst_t), .up(1'b1), .count(1'b1), .clk(clk), .carry(carry), .Q(out_2));  // open: load, D
  // ROM #(.line("quad"), .misaligned("true")) rom_1: pin names not known; wires that end beside it: current_pc_if[7:0], inst[7:0], inst[15:8], inst[23:16], inst[31:24]
  // Probe on inst

  // Notes on the sheet:
  //   DON'T TOUCH!
  //   IF stage output
  //   MEM stage output
  //   WB stage output
  //   contents of rom_1 (hex, n*v repeats v):
  //   93 2 10 0 13 3 30 0 13 5 0 0 33 5 55 0 93 82 12 0 63 84 62 0 6f f0 5f ff 13 0 0 0 13 0 0 0 13 0 0 0
  //   73 0 10
  //   test
endmodule
